# Fritzing sketch arduino and LM 35 (saved by Fritzing 0.9.3b)

parts:
  T1 = LM35 Temperature Sensor [package="TO92 [THT]"]
  Part1 = Arduino Uno (Rev3)

nets:
  N1: T1.+Vs, Part1.5V
  N2: T1.Vout, Part1.A0
  GND: T1.GND, Part1.GND

notes:
  LM35 TEMPERATURE SENSOR
